# Fritzing sketch circuit (saved by Fritzing 1.0.5)

parts:
  M1 = DOIT Esp32 DevKit v1 (30 pins long, 11 pins width) [part_number=ESP32S-PIN30]
  L298N1 = L298N DC motor driver
  PART1 = Polymer Lithium Ion Battery - Generic
  M2 = DC Motor [voltage_(max)=6V voltage_(min)=3V]
  M3 = DC Motor [voltage_(max)=6V voltage_(min)=3V]

nets:
  GND: M1.GND, L298N1.GND, PART1.GND
  N1: M1.D5, L298N1.IN1
  N2: M1.D18, L298N1.IN2
  N3: M1.D19, L298N1.IN3
  N4: M1.D21, L298N1.IN4
  N5: M1.VIN, L298N1.5V#7
  N6: L298N1.OUT1, M3.pin_2
  N7: L298N1.OUT2, M3.pin_1
  N8: L298N1.OUT3, M2.pin_2
  N9: L298N1.OUT4, M2.pin_1
  12V: L298N1.12V, PART1.VCC
  N10: L298N1.5V#9, L298N1.ENA
  N11: L298N1.5V#10, L298N1.ENB

custom parts:
  DOIT Esp32 DevKit v1 (30 pins long, 11 pins width): The DOIT Esp32 DevKit v1 is one of the development board created by DOIT to evaluate the ESP-WROOM-32 module. It is based on the ESP32 microcontroller that boasts Wifi, Bluetooth, Ethernet and Low Power support all in a single chip. (vanepp) made breadboard work, adjusted pin numbering and labels and reduced size of schematic and cleaned up pcb. This chip is 30pins long (2 x15) and 11 pins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
  L298N DC motor driver: 2x DC motor driver with 78M05 positive voltage regulator (7..35 V) L298N: max 46 V, 2 A Set 5 V Enable jumper to enable 5 V regultor (needed for the L298N) and +5 V output at screw terminal or supply external +5 V at screw terminal Set ENA and/or ENB to +5 V to enable motor permanently or supply ENA and/or ENB with PWM signal IN1 and IN2 set rotation directory for motor A (OUT1/OUT2) IN2 and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
  Polymer Lithium Ion Battery - Generic: Description: These are batteries based on the new Polymer Lithium Ion chemistry. This is the highest energy density currently in production. Comes terminated with a standard 2-pin JST-PH connector - 2mm spacing between pins. These batteries require special charging. Do not attempt to charge these with anything but a specialized LiPo charger. Battery includes built-in protection against over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
